// Logisim project Combined.circ as structural Verilog: 1 circuit, main circuit main
module main (
  input  Q0,
  input  Q0_prime,
  input  Q1,
  input  Q1_prime,
  input  Q2,
  input  Q2_prime,
  output D0,
  output D1,
  output D2
);

  wire and_1_out, and_2_out, and_3_out, and_4_out, and_5_out, and_6_out, or_1_out, or_3_out;

  and and_1 (and_1_out, Q0, Q1, Q2_prime);
  or or_1 (or_1_out, Q1_prime, Q2);
  and and_2 (and_2_out, or_1_out, Q0_prime);
  and and_3 (and_3_out, Q0, Q1);
  and and_4 (and_4_out, Q0_prime, Q2_prime);
  or or_2 (D0, and_1_out, and_2_out);
  and and_5 (and_5_out, Q2_prime, Q0_prime);
  or or_3 (or_3_out, Q0_prime, Q2);
  or or_4 (D2, and_3_out, and_4_out);
  and and_6 (and_6_out, or_3_out, Q1_prime);
  or or_5 (D1, and_5_out, and_6_out);
endmodule
