// Logisim project Final.circ as structural Verilog: 1 circuit, main circuit main
module main (
);

  wire button_1_out, clock_1_out, D0_q, D0_qn, D1_q, D1_qn, D2_q, D2_qn, main_1_d0, main_1_d1, main_1_d2,
       n7_segment_display_driver_1_p5, n7_segment_display_driver_1_p6, n7_segment_display_driver_1_p7,
       n7_segment_display_driver_1_p8, n7_segment_display_driver_1_p9, n7_segment_display_driver_1_p10,
       n7_segment_display_driver_1_p11;

  Combined_main main_1 (
    .Q0(D0_q), .Q0_prime(D0_qn), .Q1(D1_q), .Q1_prime(D1_qn), .Q2(D2_q), .Q2_prime(D2_qn), .D0(main_1_d0),
    .D1(main_1_d1), .D2(main_1_d2));
  Clock clock_1 (.out(clock_1_out));
  D_Flip_Flop D0 (.clk(clock_1_out), .D(main_1_d0), .Q(D0_q), .Qn(D0_qn), .preset(button_1_out));  // open: en, reset
  D_Flip_Flop D1 (.clk(clock_1_out), .D(main_1_d1), .Q(D1_q), .Qn(D1_qn));  // open: preset, en, reset
  D_Flip_Flop D2 (.clk(clock_1_out), .D(main_1_d2), .Q(D2_q), .Qn(D2_qn), .preset(button_1_out));  // open: en, reset
  Button button_1 (.out(button_1_out));
  // _7_segment_display_driver 7_segment_display_driver_1: pin names not known; wires that end beside it: 1'b0, D2_q, D1_q, D0_q, n7_segment_display_driver_1_p5, n7_segment_display_driver_1_p6, n7_segment_display_driver_1_p7, n7_segment_display_driver_1_p8, n7_segment_display_driver_1_p9, n7_segment_display_driver_1_p10, n7_segment_display_driver_1_p11
  _7_Segment_Display u_7_segment_display_1 (
    .g(n7_segment_display_driver_1_p11), .f(n7_segment_display_driver_1_p10),
    .a(n7_segment_display_driver_1_p5), .b(n7_segment_display_driver_1_p6),
    .e(n7_segment_display_driver_1_p9), .d(n7_segment_display_driver_1_p8), .c(n7_segment_display_driver_1_p7));  // open: dp
endmodule
